// Logisim project 实验3-CS190X-U2019XXXXX-XX.circ as structural Verilog: 6 circuits, main circuit 四位乘法器
module \四位乘法器  (
  input  [3:0] a,
  input  [3:0] b,
  output [7:0] P
);

  wire [7:0] adder_1_out, adder_2_out, adder_3_out, adder_4_out, bit_extender_1_out, multiplexer_1_out,
       multiplexer_2_out, multiplexer_3_out, shifter_1_out, shifter_2_out, shifter_3_out, shifter_4_out;

  assign bit_extender_1_out = {{4{1'b0}}, b};  // Bit_Extender bit_extender_1
  Adder adder_1 (.a({8{1'b0}}), .b(bit_extender_1_out), .out(adder_1_out));  // open: cin, cout
  Multiplexer #(.width(8), .enable("false")) multiplexer_1 (
    .in0({8{1'b0}}), .in1(adder_1_out), .out(multiplexer_1_out), .sel(a[0]));
  Shifter shifter_1 (.in(bit_extender_1_out), .\dist (3'b001), .out(shifter_1_out));
  Adder adder_2 (.a(multiplexer_1_out), .b(shifter_1_out), .out(adder_2_out));  // open: cin, cout
  Multiplexer #(.width(8), .enable("false")) multiplexer_2 (
    .in0(multiplexer_1_out), .in1(adder_2_out), .out(multiplexer_2_out), .sel(a[1]));
  Shifter shifter_2 (.in(shifter_1_out), .\dist (3'b001), .out(shifter_2_out));
  Adder adder_3 (.a(multiplexer_2_out), .b(shifter_2_out), .out(adder_3_out));  // open: cin, cout
  Multiplexer #(.width(8), .enable("false")) multiplexer_3 (
    .in0(multiplexer_2_out), .in1(adder_3_out), .out(multiplexer_3_out), .sel(a[2]));
  Shifter shifter_3 (.in(shifter_2_out), .\dist (3'b001), .out(shifter_3_out));
  Adder adder_4 (.a(multiplexer_3_out), .b(shifter_3_out), .out(adder_4_out));  // open: cin, cout
  Multiplexer #(.width(8), .enable("false")) multiplexer_4 (
    .in0(multiplexer_3_out), .in1(adder_4_out), .out(P), .sel(a[3]));
  Shifter shifter_4 (.in(shifter_3_out), .\dist (3'b001), .out(shifter_4_out));
  Shifter shifter_5 (.in(shifter_4_out), .\dist (3'b001));  // open: out
endmodule

module \四位乘法器测试电路  (
  input  [3:0] a_3_0,
  input  [3:0] b_3_0,
  output [7:0] P_7_0
);

  \四位乘法器  \u_四位乘法器_1  (.b(b_3_0), .P(P_7_0), .a(a_3_0));
endmodule

module \_32X4乘法器  (
  input  [3:0] in_1,
  input  [31:0] in_2,
  output [31:0] P,
  output [31:0] P_2
);

  wire adder_9_cout;
  wire [31:0] adder_1_out, adder_2_out, adder_3_out, adder_4_out, adder_5_out, adder_6_out, adder_7_out,
       adder_8_out, bit_extender_1_out, bit_extender_2_out, bit_extender_3_out, bit_extender_4_out,
       multiplexer_1_out, multiplexer_2_out, multiplexer_3_out, multiplexer_4_out, multiplexer_5_out,
       multiplexer_6_out, multiplexer_7_out, multiplexer_8_out, shifter_1_out, shifter_2_out, shifter_3_out,
       shifter_4_out, shifter_5_out, shifter_6_out, shifter_7_out, shifter_8_out, shifter_11_out;

  assign bit_extender_1_out = {{16{1'b0}}, in_2[15:0]};  // Bit_Extender bit_extender_1
  assign bit_extender_2_out = {{16{1'b0}}, in_2[31:16]};  // Bit_Extender bit_extender_2
  Adder #(.width(32)) adder_1 (.a({32{1'b0}}), .b(bit_extender_1_out), .out(adder_1_out));  // open: cin, cout
  Adder #(.width(32)) adder_2 (.a({32{1'b0}}), .b(bit_extender_2_out), .out(adder_2_out));  // open: cin, cout
  Multiplexer #(.width(32), .enable("false")) multiplexer_1 (
    .in0({32{1'b0}}), .in1(adder_2_out), .out(multiplexer_1_out), .sel(in_1[0]));
  Multiplexer #(.width(32), .enable("false")) multiplexer_2 (
    .in0({32{1'b0}}), .in1(adder_1_out), .out(multiplexer_2_out), .sel(in_1[0]));
  Shifter #(.width(32)) shifter_1 (.in(bit_extender_1_out), .\dist (5'b00001), .out(shifter_1_out));
  Shifter #(.width(32)) shifter_2 (.in(bit_extender_2_out), .\dist (5'b00001), .out(shifter_2_out));
  Adder #(.width(32)) adder_3 (.a(multiplexer_2_out), .b(shifter_1_out), .out(adder_3_out));  // open: cin, cout
  Adder #(.width(32)) adder_4 (.a(multiplexer_1_out), .b(shifter_2_out), .out(adder_4_out));  // open: cin, cout
  Multiplexer #(.width(32), .enable("false")) multiplexer_3 (
    .in0(multiplexer_2_out), .in1(adder_3_out), .out(multiplexer_3_out), .sel(in_1[1]));
  Shifter #(.width(32)) shifter_3 (.in(shifter_1_out), .\dist (5'b00001), .out(shifter_3_out));
  Multiplexer #(.width(32), .enable("false")) multiplexer_4 (
    .in0(multiplexer_1_out), .in1(adder_4_out), .out(multiplexer_4_out), .sel(in_1[1]));
  Shifter #(.width(32)) shifter_4 (.in(shifter_2_out), .\dist (5'b00001), .out(shifter_4_out));
  Adder #(.width(32)) adder_5 (.a(multiplexer_3_out), .b(shifter_3_out), .out(adder_5_out));  // open: cin, cout
  Adder #(.width(32)) adder_6 (.a(multiplexer_4_out), .b(shifter_4_out), .out(adder_6_out));  // open: cin, cout
  Multiplexer #(.width(32), .enable("false")) multiplexer_5 (
    .in0(multiplexer_3_out), .in1(adder_5_out), .out(multiplexer_5_out), .sel(in_1[2]));
  Shifter #(.width(32)) shifter_5 (.in(shifter_3_out), .\dist (5'b00001), .out(shifter_5_out));
  Multiplexer #(.width(32), .enable("false")) multiplexer_6 (
    .in0(multiplexer_4_out), .in1(adder_6_out), .out(multiplexer_6_out), .sel(in_1[2]));
  Shifter #(.width(32)) shifter_6 (.in(shifter_4_out), .\dist (5'b00001), .out(shifter_6_out));
  Adder #(.width(32)) adder_7 (.a(multiplexer_5_out), .b(shifter_5_out), .out(adder_7_out));  // open: cin, cout
  Adder #(.width(32)) adder_8 (.a(multiplexer_6_out), .b(shifter_6_out), .out(adder_8_out));  // open: cin, cout
  Multiplexer #(.width(32), .enable("false")) multiplexer_7 (
    .in0(multiplexer_5_out), .in1(adder_7_out), .out(multiplexer_7_out), .sel(in_1[3]));
  Shifter #(.width(32)) shifter_7 (.in(shifter_5_out), .\dist (5'b00001), .out(shifter_7_out));
  Multiplexer #(.width(32), .enable("false")) multiplexer_8 (
    .in0(multiplexer_6_out), .in1(adder_8_out), .out(multiplexer_8_out), .sel(in_1[3]));
  Shifter #(.width(32)) shifter_8 (.in(shifter_6_out), .\dist (5'b00001), .out(shifter_8_out));
  Shifter #(.width(32)) shifter_9 (.in(shifter_7_out), .\dist (5'b00001));  // open: out
  Shifter #(.width(32)) shifter_10 (.in(shifter_8_out), .\dist (5'b00001));  // open: out
  assign bit_extender_3_out = {{16{1'b0}}, multiplexer_8_out[15:0]};  // Bit_Extender bit_extender_3
  assign bit_extender_4_out = {{16{1'b0}}, multiplexer_8_out[31:16]};  // Bit_Extender bit_extender_4
  Shifter #(.width(32)) shifter_11 (.in(bit_extender_3_out), .\dist (5'b10000), .out(shifter_11_out));
  Adder #(.width(32)) adder_9 (.a(multiplexer_7_out), .b(shifter_11_out), .out(P), .cout(adder_9_cout));  // open: cin
  Adder #(.width(32)) adder_10 (.a(bit_extender_4_out), .b({32{1'b0}}), .out(P_2), .cin(adder_9_cout));  // open: cout
endmodule

module \_32X4乘法器测试电路  (
  input  [3:0] a_3_0,
  input  [31:0] b_31_0,
  output [31:0] pl_31_0,
  output [31:0] ph_31_0
);

  \_32X4乘法器  \u_32x4乘法器_1  (.in_2(b_31_0), .P(pl_31_0), .P_2(ph_31_0), .in_1(a_3_0));
endmodule

module \_32X32乘法器  (
  input  [31:0] a_31_0,
  input  [31:0] b_31_0,
  output [31:0] pl_31_0,
  output [31:0] ph_31_0
);

  wire adder_1_cout, adder_3_cout, adder_5_cout, adder_7_cout, adder_9_cout, adder_11_cout, adder_13_cout;
  wire [3:0] \n32x4乘法器_1_p_2 , \n32x4乘法器_1_p_2_2 , \n32x4乘法器_1_p_2_3 , \n32x4乘法器_1_p_2_5 ,
       \n32x4乘法器_1_p_2_6 , \n32x4乘法器_2_p_2_2 , \n32x4乘法器_2_p_2_3 , \n32x4乘法器_2_p_2_4 , \n32x4乘法器_2_p_2_5 ,
       \n32x4乘法器_2_p_2_6 , \n32x4乘法器_3_p_2_2 , \n32x4乘法器_3_p_2_3 , \n32x4乘法器_3_p_2_4 , \n32x4乘法器_3_p_2_5 ,
       \n32x4乘法器_3_p_2_6 , \n32x4乘法器_4_p_2 , \n32x4乘法器_4_p_2_2 , \n32x4乘法器_4_p_2_4 , \n32x4乘法器_4_p_2_5 ,
       \n32x4乘法器_4_p_2_6 , \n32x4乘法器_4_p_2_7 , \n32x4乘法器_5_p_2 , \n32x4乘法器_5_p_2_3 , \n32x4乘法器_5_p_2_4 ,
       \n32x4乘法器_5_p_2_5 , \n32x4乘法器_5_p_2_6 , \n32x4乘法器_5_p_2_7 , \n32x4乘法器_6_p_2 , \n32x4乘法器_6_p_2_2 ,
       \n32x4乘法器_6_p_2_3 , \n32x4乘法器_6_p_2_4 , \n32x4乘法器_6_p_2_5 ;
  wire [7:0] \n32x4乘法器_4_p_2_3 , \n32x4乘法器_5_p_2_2 ;
  wire [11:0] \n32x4乘法器_1_p_2_4 , \n32x4乘法器_2_p_2 , \n32x4乘法器_3_p_2 , \n32x4乘法器_6_p_2_6 ;
  wire [31:0] adder_1_out, adder_2_out, adder_3_out, adder_4_out, adder_5_out, adder_6_out, adder_7_out,
       adder_8_out, adder_9_out, adder_10_out, adder_11_out, adder_12_out, \n32x4乘法器_1_p , \n32x4乘法器_2_p ,
       \n32x4乘法器_5_p , \n32x4乘法器_6_p , \n32x4乘法器_7_p , \n32x4乘法器_7_p_2 , \n32x4乘法器_8_p , \n32x4乘法器_8_p_2 ;
  wire [31:8] \n32x4乘法器_3_p , \n32x4乘法器_4_p_3 ;
  wire [31:24] \n32x4乘法器_3_p_3 , \n32x4乘法器_4_p ;

  \_32X4乘法器  \u_32x4乘法器_1  (
    .in_2(b_31_0), .P(\n32x4乘法器_1_p ),
    .P_2({\n32x4乘法器_1_p_2_3 , \n32x4乘法器_1_p_2_2 , \n32x4乘法器_1_p_2 , \n32x4乘法器_1_p_2_6 , \n32x4乘法器_1_p_2_5 , \n32x4乘法器_1_p_2_4 }),
    .in_1(a_31_0[15:12]));
  \_32X4乘法器  \u_32x4乘法器_2  (
    .in_2(b_31_0), .P(\n32x4乘法器_2_p ),
    .P_2({\n32x4乘法器_2_p_2_6 , \n32x4乘法器_2_p_2_5 , \n32x4乘法器_2_p_2_4 , \n32x4乘法器_2_p_2_3 , \n32x4乘法器_2_p_2_2 , \n32x4乘法器_2_p_2 }),
    .in_1(a_31_0[31:28]));
  \_32X4乘法器  \u_32x4乘法器_3  (
    .in_2(b_31_0), .P({\n32x4乘法器_3_p , \n32x4乘法器_3_p_3 }),
    .P_2({\n32x4乘法器_3_p_2_6 , \n32x4乘法器_3_p_2_5 , \n32x4乘法器_3_p_2_4 , \n32x4乘法器_3_p_2_3 , \n32x4乘法器_3_p_2_2 , \n32x4乘法器_3_p_2 }),
    .in_1(a_31_0[27:24]));
  \_32X4乘法器  \u_32x4乘法器_4  (
    .in_2(b_31_0), .P({\n32x4乘法器_4_p , \n32x4乘法器_4_p_3 }),
    .P_2({\n32x4乘法器_4_p_2_2 , \n32x4乘法器_4_p_2 , \n32x4乘法器_4_p_2_7 , \n32x4乘法器_4_p_2_6 , \n32x4乘法器_4_p_2_5 , \n32x4乘法器_4_p_2_4 , \n32x4乘法器_4_p_2_3 }),
    .in_1(a_31_0[11:8]));
  \_32X4乘法器  \u_32x4乘法器_5  (
    .in_2(b_31_0), .P(\n32x4乘法器_5_p ),
    .P_2({\n32x4乘法器_5_p_2 , \n32x4乘法器_5_p_2_7 , \n32x4乘法器_5_p_2_6 , \n32x4乘法器_5_p_2_5 , \n32x4乘法器_5_p_2_4 , \n32x4乘法器_5_p_2_3 , \n32x4乘法器_5_p_2_2 }),
    .in_1(a_31_0[7:4]));
  \_32X4乘法器  \u_32x4乘法器_6  (
    .in_2(b_31_0), .P(\n32x4乘法器_6_p ),
    .P_2({\n32x4乘法器_6_p_2_5 , \n32x4乘法器_6_p_2_4 , \n32x4乘法器_6_p_2_3 , \n32x4乘法器_6_p_2_2 , \n32x4乘法器_6_p_2 , \n32x4乘法器_6_p_2_6 }),
    .in_1(a_31_0[23:20]));
  \_32X4乘法器  \u_32x4乘法器_7  (.in_2(b_31_0), .P(\n32x4乘法器_7_p ), .P_2(\n32x4乘法器_7_p_2 ), .in_1(a_31_0[3:0]));
  Adder #(.width(32)) adder_1 (
    .a({\n32x4乘法器_4_p_3 , {8{1'b0}}}), .b({\n32x4乘法器_1_p [19:0], {12{1'b0}}}), .out(adder_1_out),
    .cout(adder_1_cout));  // open: cin
  Adder #(.width(32)) adder_2 (
    .a({\n32x4乘法器_4_p_2_7 , \n32x4乘法器_4_p_2_6 , \n32x4乘法器_4_p_2_5 , \n32x4乘法器_4_p_2_4 , \n32x4乘法器_4_p_2_3 , \n32x4乘法器_4_p }),
    .b({\n32x4乘法器_1_p_2_6 , \n32x4乘法器_1_p_2_5 , \n32x4乘法器_1_p_2_4 , \n32x4乘法器_1_p [31:20]}),
    .out(adder_2_out), .cin(adder_1_cout));  // open: cout
  \_32X4乘法器  \u_32x4乘法器_8  (.in_2(b_31_0), .P(\n32x4乘法器_8_p ), .P_2(\n32x4乘法器_8_p_2 ), .in_1(a_31_0[19:16]));
  Adder #(.width(32)) adder_3 (
    .a(\n32x4乘法器_7_p ), .b({\n32x4乘法器_5_p [27:0], 4'b0000}), .out(adder_3_out), .cout(adder_3_cout));  // open: cin
  Adder #(.width(32)) adder_4 (
    .a(\n32x4乘法器_7_p_2 ),
    .b({\n32x4乘法器_5_p_2_7 , \n32x4乘法器_5_p_2_6 , \n32x4乘法器_5_p_2_5 , \n32x4乘法器_5_p_2_4 , \n32x4乘法器_5_p_2_3 , \n32x4乘法器_5_p_2_2 , \n32x4乘法器_5_p [31:28]}),
    .out(adder_4_out), .cin(adder_3_cout));  // open: cout
  Adder #(.width(32)) adder_5 (.a(adder_3_out), .b(adder_1_out), .out(adder_5_out), .cout(adder_5_cout));  // open: cin
  Adder #(.width(32)) adder_6 (.a(adder_4_out), .b(adder_2_out), .out(adder_6_out), .cin(adder_5_cout));  // open: cout
  Adder #(.width(32)) adder_7 (
    .a({\n32x4乘法器_8_p [15:0], {16{1'b0}}}), .b({\n32x4乘法器_6_p [11:0], {20{1'b0}}}), .out(adder_7_out),
    .cout(adder_7_cout));  // open: cin
  Adder #(.width(32)) adder_8 (
    .a({\n32x4乘法器_8_p_2 [15:0], \n32x4乘法器_8_p [31:16]}), .b({\n32x4乘法器_6_p_2_6 , \n32x4乘法器_6_p [31:12]}),
    .out(adder_8_out), .cin(adder_7_cout));  // open: cout
  Adder #(.width(32)) adder_9 (
    .a({\n32x4乘法器_3_p_3 , {24{1'b0}}}), .b({\n32x4乘法器_2_p [3:0], {28{1'b0}}}), .out(adder_9_out),
    .cout(adder_9_cout));  // open: cin
  Adder #(.width(32)) adder_10 (
    .a({\n32x4乘法器_3_p_2 [7:0], \n32x4乘法器_3_p }), .b({\n32x4乘法器_2_p_2 [3:0], \n32x4乘法器_2_p [31:4]}),
    .out(adder_10_out), .cin(adder_9_cout));  // open: cout
  Adder #(.width(32)) adder_11 (
    .a(adder_7_out), .b(adder_9_out), .out(adder_11_out), .cout(adder_11_cout));  // open: cin
  Adder #(.width(32)) adder_12 (
    .a(adder_8_out), .b(adder_10_out), .out(adder_12_out), .cin(adder_11_cout));  // open: cout
  Adder #(.width(32)) adder_13 (.a(adder_5_out), .b(adder_11_out), .out(pl_31_0), .cout(adder_13_cout));  // open: cin
  Adder #(.width(32)) adder_14 (.a(adder_6_out), .b(adder_12_out), .out(ph_31_0), .cin(adder_13_cout));  // open: cout
endmodule

module \_32X32乘法器测试电路  (
  input  [31:0] a_31_0,
  input  [31:0] b_31_0,
  output [31:0] pl_31_0,
  output [31:0] ph_31_0
);

  \_32X32乘法器  \u_32x32乘法器_1  (.a_31_0(a_31_0), .b_31_0(b_31_0), .pl_31_0(pl_31_0), .ph_31_0(ph_31_0));
endmodule
