// Logisim project 实验4-CS190X-U2019XXXXX-XX.circ as structural Verilog: 5 circuits, main circuit 四位除法器
module \四位除法器  (
  input  [3:0] n2,
  input  [3:0] d,
  output [3:0] quot,
  output [3:0] rem
);

  wire comparator_1_eq, comparator_1_gt, comparator_2_eq, comparator_2_gt, comparator_3_eq, comparator_3_gt,
       comparator_4_eq, comparator_4_gt, or_1_out, or_2_out, or_3_out, or_4_out;
  wire [0:0] multiplexer_5_out_2;
  wire [1:1] multiplexer_3_out_2;
  wire [2:2] multiplexer_1_out_2;
  wire [3:0] multiplexer_1_out, multiplexer_3_out, multiplexer_4_out, subtractor_1_out, subtractor_2_out,
       subtractor_3_out, subtractor_4_out;
  wire [3:1] multiplexer_5_out;
  wire [7:0] multiplexer_6_out, shifter_1_out, shifter_2_out, shifter_4_out;
  wire [7:4] multiplexer_2_out, shifter_3_out;

  Shifter shifter_1 (.in({4'b0000, n2}), .\dist (3'b001), .out(shifter_1_out));
  Shifter shifter_2 (.in({multiplexer_2_out, shifter_1_out[3:0]}), .\dist (3'b001), .out(shifter_2_out));
  Shifter shifter_3 (
    .in({multiplexer_4_out, shifter_2_out[3:0]}), .\dist (3'b001),
    .out({shifter_3_out, multiplexer_6_out[3:0]}));
  Shifter shifter_4 (.in(multiplexer_6_out), .\dist (3'b001), .out(shifter_4_out));
  Subtractor #(.width(4)) subtractor_1 (.a(shifter_1_out[7:4]), .b(d), .out(subtractor_1_out));  // open: bin, bout
  Comparator #(.width(4), .mode("unsigned")) comparator_1 (
    .a(shifter_1_out[7:4]), .b(d), .gt(comparator_1_gt), .eq(comparator_1_eq));  // open: lt
  Subtractor #(.width(4)) subtractor_2 (.a(shifter_2_out[7:4]), .b(d), .out(subtractor_2_out));  // open: bin, bout
  Comparator #(.width(4), .mode("unsigned")) comparator_2 (
    .a(shifter_2_out[7:4]), .b(d), .gt(comparator_2_gt), .eq(comparator_2_eq));  // open: lt
  Subtractor #(.width(4)) subtractor_3 (.a(shifter_3_out), .b(d), .out(subtractor_3_out));  // open: bin, bout
  Comparator #(.width(4), .mode("unsigned")) comparator_3 (
    .a(shifter_3_out), .b(d), .gt(comparator_3_gt), .eq(comparator_3_eq));  // open: lt
  Subtractor #(.width(4)) subtractor_4 (.a(shifter_4_out[7:4]), .b(d), .out(subtractor_4_out));  // open: bin, bout
  Comparator #(.width(4), .mode("unsigned")) comparator_4 (
    .a(shifter_4_out[7:4]), .b(d), .gt(comparator_4_gt), .eq(comparator_4_eq));  // open: lt
  Multiplexer #(.width(4), .enable("false")) multiplexer_1 (
    .in0(4'b0000), .in1(4'b1000),
    .out({multiplexer_1_out[3], multiplexer_1_out_2[2], multiplexer_1_out[1:0]}), .sel(or_1_out));
  Multiplexer #(.width(4), .enable("false")) multiplexer_2 (
    .in0(shifter_1_out[7:4]), .in1(subtractor_1_out), .out(multiplexer_2_out), .sel(or_1_out));
  or or_1 (or_1_out, comparator_1_gt, comparator_1_eq);
  Multiplexer #(.width(4), .enable("false")) multiplexer_3 (
    .in0({multiplexer_1_out[3], multiplexer_1_out_2[2], multiplexer_1_out[1:0]}),
    .in1({multiplexer_1_out[3], 1'b1, multiplexer_1_out[1:0]}),
    .out({multiplexer_3_out[3:2], multiplexer_3_out_2[1], multiplexer_3_out[0]}), .sel(or_2_out));
  Multiplexer #(.width(4), .enable("false")) multiplexer_4 (
    .in0(shifter_2_out[7:4]), .in1(subtractor_2_out), .out(multiplexer_4_out), .sel(or_2_out));
  or or_2 (or_2_out, comparator_2_gt, comparator_2_eq);
  Multiplexer #(.width(4), .enable("false")) multiplexer_5 (
    .in0({multiplexer_3_out[3:2], multiplexer_3_out_2[1], multiplexer_3_out[0]}),
    .in1({multiplexer_3_out[3:2], 1'b1, multiplexer_3_out[0]}),
    .out({multiplexer_5_out, multiplexer_5_out_2[0]}), .sel(or_3_out));
  Multiplexer #(.width(4), .enable("false")) multiplexer_6 (
    .in0(shifter_3_out), .in1(subtractor_3_out), .out(multiplexer_6_out[7:4]), .sel(or_3_out));
  or or_3 (or_3_out, comparator_3_gt, comparator_3_eq);
  Multiplexer #(.width(4), .enable("false")) multiplexer_7 (
    .in0({multiplexer_5_out, multiplexer_5_out_2[0]}), .in1({multiplexer_5_out, 1'b1}), .out(quot),
    .sel(or_4_out));
  Multiplexer #(.width(4), .enable("false")) multiplexer_8 (
    .in0(shifter_4_out[7:4]), .in1(subtractor_4_out), .out(rem), .sel(or_4_out));
  or or_4 (or_4_out, comparator_4_gt, comparator_4_eq);
endmodule

module \四位除法器测试电路  (
  input  [3:0] n2_3_0,
  input  [3:0] d_3_0,
  output [3:0] quot_3_0,
  output [3:0] rem_3_0
);

  \四位除法器  \u_四位除法器_1  (.n2(n2_3_0), .d(d_3_0), .quot(quot_3_0), .rem(rem_3_0));
endmodule

module \_32位除法器  (
  input  [31:0] d,
  input  [31:0] n,
  output [31:0] rem,
  output [31:0] quot
);

  wire [31:0] n32div_1_1_next_quot, n32div_1_1_next_rem, n32div_1_3_next_quot, n32div_1_3_next_rem,
       n32div_1_4_next_quot, n32div_1_4_next_rem, n32div_1_5_next_quot, n32div_1_5_next_rem,
       n32div_1_6_next_quot, n32div_1_6_next_rem, n32div_1_7_next_quot, n32div_1_7_next_rem,
       n32div_1_8_next_quot, n32div_1_8_next_rem, n32div_1_9_next_quot, n32div_1_9_next_rem,
       n32div_1_10_next_quot, n32div_1_10_next_rem, n32div_1_11_next_quot, n32div_1_11_next_rem,
       n32div_1_12_next_quot, n32div_1_12_next_rem, n32div_1_13_next_quot, n32div_1_13_next_rem,
       n32div_1_14_next_quot, n32div_1_14_next_rem, n32div_1_15_next_quot, n32div_1_15_next_rem,
       n32div_1_16_next_quot, n32div_1_16_next_rem, n32div_1_17_next_quot, n32div_1_17_next_rem,
       n32div_1_18_next_quot, n32div_1_18_next_rem, n32div_1_19_next_quot, n32div_1_19_next_rem,
       n32div_1_20_next_quot, n32div_1_20_next_rem, n32div_1_21_next_quot, n32div_1_21_next_rem,
       n32div_1_22_next_quot, n32div_1_22_next_rem, n32div_1_23_next_quot, n32div_1_23_next_rem,
       n32div_1_24_next_quot, n32div_1_24_next_rem, n32div_1_25_next_quot, n32div_1_25_next_rem,
       n32div_1_26_next_quot, n32div_1_26_next_rem, n32div_1_27_next_quot, n32div_1_27_next_rem,
       n32div_1_28_next_quot, n32div_1_28_next_rem, n32div_1_29_next_quot, n32div_1_29_next_rem,
       n32div_1_30_next_quot, n32div_1_30_next_rem, n32div_1_31_next_quot, n32div_1_31_next_rem,
       n32div_1_32_next_quot, n32div_1_32_next_rem;

  _32div_1 u_32div_1_1 (
    .d(d), .cur_rem(n32div_1_5_next_rem), .cur_quot(n32div_1_5_next_quot), .next_rem(n32div_1_1_next_rem),
    .next_quot(n32div_1_1_next_quot));
  _32div_1 u_32div_1_2 (
    .d(d), .cur_rem(n32div_1_6_next_rem), .cur_quot(n32div_1_6_next_quot), .next_rem(rem), .next_quot(quot));
  _32div_1 u_32div_1_3 (
    .d(d), .cur_rem({32{1'b0}}), .cur_quot(n), .next_rem(n32div_1_3_next_rem),
    .next_quot(n32div_1_3_next_quot));
  _32div_1 u_32div_1_4 (
    .d(d), .cur_rem(n32div_1_1_next_rem), .cur_quot(n32div_1_1_next_quot), .next_rem(n32div_1_4_next_rem),
    .next_quot(n32div_1_4_next_quot));
  _32div_1 u_32div_1_5 (
    .d(d), .cur_rem(n32div_1_8_next_rem), .cur_quot(n32div_1_8_next_quot), .next_rem(n32div_1_5_next_rem),
    .next_quot(n32div_1_5_next_quot));
  _32div_1 u_32div_1_6 (
    .d(d), .cur_rem(n32div_1_10_next_rem), .cur_quot(n32div_1_10_next_quot), .next_rem(n32div_1_6_next_rem),
    .next_quot(n32div_1_6_next_quot));
  _32div_1 u_32div_1_7 (
    .d(d), .cur_rem(n32div_1_3_next_rem), .cur_quot(n32div_1_3_next_quot), .next_rem(n32div_1_7_next_rem),
    .next_quot(n32div_1_7_next_quot));
  _32div_1 u_32div_1_8 (
    .d(d), .cur_rem(n32div_1_13_next_rem), .cur_quot(n32div_1_13_next_quot), .next_rem(n32div_1_8_next_rem),
    .next_quot(n32div_1_8_next_quot));
  _32div_1 u_32div_1_9 (
    .d(d), .cur_rem(n32div_1_4_next_rem), .cur_quot(n32div_1_4_next_quot), .next_rem(n32div_1_9_next_rem),
    .next_quot(n32div_1_9_next_quot));
  _32div_1 u_32div_1_10 (
    .d(d), .cur_rem(n32div_1_14_next_rem), .cur_quot(n32div_1_14_next_quot), .next_rem(n32div_1_10_next_rem),
    .next_quot(n32div_1_10_next_quot));
  _32div_1 u_32div_1_11 (
    .d(d), .cur_rem(n32div_1_7_next_rem), .cur_quot(n32div_1_7_next_quot), .next_rem(n32div_1_11_next_rem),
    .next_quot(n32div_1_11_next_quot));
  _32div_1 u_32div_1_12 (
    .d(d), .cur_rem(n32div_1_9_next_rem), .cur_quot(n32div_1_9_next_quot), .next_rem(n32div_1_12_next_rem),
    .next_quot(n32div_1_12_next_quot));
  _32div_1 u_32div_1_13 (
    .d(d), .cur_rem(n32div_1_17_next_rem), .cur_quot(n32div_1_17_next_quot), .next_rem(n32div_1_13_next_rem),
    .next_quot(n32div_1_13_next_quot));
  _32div_1 u_32div_1_14 (
    .d(d), .cur_rem(n32div_1_18_next_rem), .cur_quot(n32div_1_18_next_quot), .next_rem(n32div_1_14_next_rem),
    .next_quot(n32div_1_14_next_quot));
  _32div_1 u_32div_1_15 (
    .d(d), .cur_rem(n32div_1_11_next_rem), .cur_quot(n32div_1_11_next_quot), .next_rem(n32div_1_15_next_rem),
    .next_quot(n32div_1_15_next_quot));
  _32div_1 u_32div_1_16 (
    .d(d), .cur_rem(n32div_1_12_next_rem), .cur_quot(n32div_1_12_next_quot), .next_rem(n32div_1_16_next_rem),
    .next_quot(n32div_1_16_next_quot));
  _32div_1 u_32div_1_17 (
    .d(d), .cur_rem(n32div_1_21_next_rem), .cur_quot(n32div_1_21_next_quot), .next_rem(n32div_1_17_next_rem),
    .next_quot(n32div_1_17_next_quot));
  _32div_1 u_32div_1_18 (
    .d(d), .cur_rem(n32div_1_22_next_rem), .cur_quot(n32div_1_22_next_quot), .next_rem(n32div_1_18_next_rem),
    .next_quot(n32div_1_18_next_quot));
  _32div_1 u_32div_1_19 (
    .d(d), .cur_rem(n32div_1_15_next_rem), .cur_quot(n32div_1_15_next_quot), .next_rem(n32div_1_19_next_rem),
    .next_quot(n32div_1_19_next_quot));
  _32div_1 u_32div_1_20 (
    .d(d), .cur_rem(n32div_1_16_next_rem), .cur_quot(n32div_1_16_next_quot), .next_rem(n32div_1_20_next_rem),
    .next_quot(n32div_1_20_next_quot));
  _32div_1 u_32div_1_21 (
    .d(d), .cur_rem(n32div_1_24_next_rem), .cur_quot(n32div_1_24_next_quot), .next_rem(n32div_1_21_next_rem),
    .next_quot(n32div_1_21_next_quot));
  _32div_1 u_32div_1_22 (
    .d(d), .cur_rem(n32div_1_26_next_rem), .cur_quot(n32div_1_26_next_quot), .next_rem(n32div_1_22_next_rem),
    .next_quot(n32div_1_22_next_quot));
  _32div_1 u_32div_1_23 (
    .d(d), .cur_rem(n32div_1_19_next_rem), .cur_quot(n32div_1_19_next_quot), .next_rem(n32div_1_23_next_rem),
    .next_quot(n32div_1_23_next_quot));
  _32div_1 u_32div_1_24 (
    .d(d), .cur_rem(n32div_1_29_next_rem), .cur_quot(n32div_1_29_next_quot), .next_rem(n32div_1_24_next_rem),
    .next_quot(n32div_1_24_next_quot));
  _32div_1 u_32div_1_25 (
    .d(d), .cur_rem(n32div_1_20_next_rem), .cur_quot(n32div_1_20_next_quot), .next_rem(n32div_1_25_next_rem),
    .next_quot(n32div_1_25_next_quot));
  _32div_1 u_32div_1_26 (
    .d(d), .cur_rem(n32div_1_30_next_rem), .cur_quot(n32div_1_30_next_quot), .next_rem(n32div_1_26_next_rem),
    .next_quot(n32div_1_26_next_quot));
  _32div_1 u_32div_1_27 (
    .d(d), .cur_rem(n32div_1_23_next_rem), .cur_quot(n32div_1_23_next_quot), .next_rem(n32div_1_27_next_rem),
    .next_quot(n32div_1_27_next_quot));
  _32div_1 u_32div_1_28 (
    .d(d), .cur_rem(n32div_1_25_next_rem), .cur_quot(n32div_1_25_next_quot), .next_rem(n32div_1_28_next_rem),
    .next_quot(n32div_1_28_next_quot));
  _32div_1 u_32div_1_29 (
    .d(d), .cur_rem(n32div_1_31_next_rem), .cur_quot(n32div_1_31_next_quot), .next_rem(n32div_1_29_next_rem),
    .next_quot(n32div_1_29_next_quot));
  _32div_1 u_32div_1_30 (
    .d(d), .cur_rem(n32div_1_32_next_rem), .cur_quot(n32div_1_32_next_quot), .next_rem(n32div_1_30_next_rem),
    .next_quot(n32div_1_30_next_quot));
  _32div_1 u_32div_1_31 (
    .d(d), .cur_rem(n32div_1_27_next_rem), .cur_quot(n32div_1_27_next_quot), .next_rem(n32div_1_31_next_rem),
    .next_quot(n32div_1_31_next_quot));
  _32div_1 u_32div_1_32 (
    .d(d), .cur_rem(n32div_1_28_next_rem), .cur_quot(n32div_1_28_next_quot), .next_rem(n32div_1_32_next_rem),
    .next_quot(n32div_1_32_next_quot));
endmodule

module \_32位除法器测试电路  (
  input  [31:0] n,
  input  [31:0] d,
  output [31:0] quot,
  output [31:0] rem
);

  \_32位除法器  \u_32位除法器_1  (.d(d), .n(n), .rem(rem), .quot(quot));
endmodule

module _32div_1 (
  input  [31:0] d,
  input  [31:0] cur_rem,
  input  [31:0] cur_quot,
  output [31:0] next_rem,
  output [31:0] next_quot
);

  wire comparator_1_gt;
  wire [31:0] or_1_out, or_2_out, shifter_1_out, shifter_2_out, shifter_3_out, subtractor_1_out;

  Shifter #(.width(32)) shifter_1 (.in(cur_rem), .\dist (5'b00001), .out(shifter_1_out));
  Shifter #(.width(32), .shift("lr")) shifter_2 (.in(cur_quot), .\dist ({5{1'b1}}), .out(shifter_2_out));
  Shifter #(.width(32)) shifter_3 (.in(cur_quot), .\dist (5'b00001), .out(shifter_3_out));
  assign or_1_out = shifter_1_out | shifter_2_out;  // OR_Gate or_1, 32 bits wide
  Comparator #(.width(32)) comparator_1 (.a(d), .b(or_1_out), .gt(comparator_1_gt));  // open: eq, lt
  Subtractor #(.width(32)) subtractor_1 (.a(or_1_out), .b(d), .out(subtractor_1_out));  // open: bin, bout
  Multiplexer #(.width(32)) multiplexer_1 (
    .in0(or_2_out), .in1(shifter_3_out), .out(next_quot), .sel(comparator_1_gt));  // open: en
  assign or_2_out = 32'h1 | shifter_3_out;  // OR_Gate or_2, 32 bits wide
  Multiplexer #(.width(32)) multiplexer_2 (
    .in0(subtractor_1_out), .in1(or_1_out), .out(next_rem), .sel(comparator_1_gt));  // open: en
endmodule
