// Logisim project 实验5-CS190X-U2019XXXXX-XX.circ as structural Verilog
// CPD
module \四位二进制可逆计数器  (
  input  CPU,
  input  CPD,
  input  CLR,
  input  \LD非 ,
  input  D,
  input  C,
  input  B,
  input  A,
  output Q3,
  output Q2,
  output Q1,
  output Q0
);

  wire and_1_out, and_2_out, and_3_out, and_4_out, and_5_out, and_6_out, and_7_out, and_8_out, and_9_out,
       and_10_out, nor_1_out, nor_2_out, nor_3_out, nor_4_out, not_1_out, not_2_out, not_3_out, not_4_out,
       not_5_out, or_1_out, or_2_out, or_3_out, or_4_out, or_5_out, or_6_out, or_7_out, or_8_out;

  and and_1 (and_1_out, Q2, Q1, Q0, CPU);
  and and_2 (and_2_out, not_3_out, not_4_out, not_5_out, CPD);
  and and_3 (and_3_out, Q1, Q0, CPU);
  and and_4 (and_4_out, not_4_out, not_5_out, CPD);
  and and_5 (and_5_out, Q0, CPU);
  and and_6 (and_6_out, not_5_out, CPD);
  not not_1 (not_1_out, \LD非 );
  nor nor_1 (nor_1_out, \LD非 , D);
  nor nor_2 (nor_2_out, \LD非 , C);
  nor nor_3 (nor_3_out, \LD非 , B);
  nor nor_4 (nor_4_out, \LD非 , A);
  or or_1 (or_1_out, and_1_out, and_2_out);
  or or_2 (or_2_out, and_3_out, and_4_out);
  or or_3 (or_3_out, and_5_out, and_6_out);
  or or_4 (or_4_out, CPU, CPD);
  and and_7 (and_7_out, not_1_out, D);
  and and_8 (and_8_out, not_1_out, C);
  and and_9 (and_9_out, not_1_out, B);
  and and_10 (and_10_out, not_1_out, A);
  or or_5 (or_5_out, CLR, nor_1_out);
  or or_6 (or_6_out, CLR, nor_2_out);
  or or_7 (or_7_out, CLR, nor_3_out);
  or or_8 (or_8_out, CLR, nor_4_out);
  D_Flip_Flop #(.trigger("falling")) d_ff_1 (
    .clk(or_1_out), .D(not_2_out), .Q(Q3), .preset(and_7_out), .reset(or_5_out));  // open: Qn, en
  D_Flip_Flop #(.trigger("falling")) d_ff_2 (
    .clk(or_2_out), .D(not_3_out), .Q(Q2), .preset(and_8_out), .reset(or_6_out));  // open: Qn, en
  D_Flip_Flop #(.trigger("falling")) d_ff_3 (
    .clk(or_3_out), .D(not_4_out), .Q(Q1), .preset(and_9_out), .reset(or_7_out));  // open: Qn, en
  D_Flip_Flop #(.trigger("falling")) d_ff_4 (
    .clk(or_4_out), .D(not_5_out), .Q(Q0), .preset(and_10_out), .reset(or_8_out));  // open: Qn, en
  not not_2 (not_2_out, Q3);
  not not_3 (not_3_out, Q2);
  not not_4 (not_4_out, Q1);
  not not_5 (not_5_out, Q0);
endmodule

module \六十进制计数器  (
  input  CPu,
  input  CLR,
  input  ADj,
  input  CPd,
  output Qcc,
  output Q1D,
  output Q1C,
  output Q1B,
  output Q1A,
  output Q0D,
  output Q0C,
  output Q0B,
  output Q0A
);

  wire and_1_out, and_2_out, and_3_out, and_4_out, and_5_out, and_6_out, and_7_out, and_8_out, d_ff_1_q,
       d_ff_2_q, nor_1_out, not_1_out, not_2_out, not_3_out, or_1_out, or_2_out, or_3_out, or_4_out,
       \四位二进制可逆计数器_1_q0 , \四位二进制可逆计数器_1_q1 , \四位二进制可逆计数器_1_q2 , \四位二进制可逆计数器_1_q3 , \四位二进制可逆计数器_2_q0 ,
       \四位二进制可逆计数器_2_q1 , \四位二进制可逆计数器_2_q2 , \四位二进制可逆计数器_2_q3 ;

  and and_1 (and_1_out, ADj, CPd);
  not not_1 (not_1_out, nor_1_out);
  or or_1 (or_1_out, CLR, d_ff_2_q);
  or or_2 (or_2_out, not_1_out, or_4_out);
  and and_2 (and_2_out, CPu, and_6_out);
  and and_3 (and_3_out, and_1_out, nor_1_out, or_4_out);
  and and_4 (and_4_out, or_2_out, or_1_out);
  and and_5 (and_5_out, and_1_out, or_2_out);
  or or_3 (or_3_out, CLR, d_ff_2_q);
  \四位二进制可逆计数器  \u_四位二进制可逆计数器_1  (
    .CLR(and_4_out), .D(1'b0), .C(1'b0), .B(1'b0), .A(1'b0), .Q3(\四位二进制可逆计数器_1_q3 ), .Q2(\四位二进制可逆计数器_1_q2 ),
    .Q1(\四位二进制可逆计数器_1_q1 ), .Q0(\四位二进制可逆计数器_1_q0 ), .\LD非 (1'b1), .CPU(CPu), .CPD(and_5_out));
  \四位二进制可逆计数器  \u_四位二进制可逆计数器_2  (
    .CLR(or_3_out), .D(1'b0), .C(1'b0), .B(1'b0), .A(1'b0), .Q3(\四位二进制可逆计数器_2_q3 ), .Q2(\四位二进制可逆计数器_2_q2 ),
    .Q1(\四位二进制可逆计数器_2_q1 ), .Q0(\四位二进制可逆计数器_2_q0 ), .\LD非 (1'b1), .CPU(and_2_out), .CPD(and_3_out));
  and and_6 (and_6_out, \四位二进制可逆计数器_1_q3 , \四位二进制可逆计数器_1_q2 , \四位二进制可逆计数器_1_q1 , \四位二进制可逆计数器_1_q0 );
  nor nor_1 (nor_1_out, \四位二进制可逆计数器_1_q3 , \四位二进制可逆计数器_1_q2 , \四位二进制可逆计数器_1_q1 , \四位二进制可逆计数器_1_q0 );
  or or_4 (or_4_out, \四位二进制可逆计数器_2_q3 , \四位二进制可逆计数器_2_q2 , \四位二进制可逆计数器_2_q1 , \四位二进制可逆计数器_2_q0 );
  not not_2 (not_2_out, \四位二进制可逆计数器_1_q0 );
  \_60以内八位二进制码转BCD码  \u_60以内八位二进制码转bcd码_1  (
    .A7(\四位二进制可逆计数器_2_q3 ), .A6(\四位二进制可逆计数器_2_q2 ), .A5(\四位二进制可逆计数器_2_q1 ), .A4(\四位二进制可逆计数器_2_q0 ),
    .A3(\四位二进制可逆计数器_1_q3 ), .A2(\四位二进制可逆计数器_1_q2 ), .A1(\四位二进制可逆计数器_1_q1 ), .A0(\四位二进制可逆计数器_1_q0 ),
    .A1D(Q1D), .A1C(Q1C), .A1B(Q1B), .A1A(Q1A), .A0D(Q0D), .A0C(Q0C), .A0B(Q0B), .A0A(Q0A));
  and and_7 (and_7_out, \四位二进制可逆计数器_1_q3 , \四位二进制可逆计数器_1_q1 , not_2_out, \四位二进制可逆计数器_2_q1 , \四位二进制可逆计数器_2_q0 );
  and and_8 (and_8_out, \四位二进制可逆计数器_1_q3 , \四位二进制可逆计数器_1_q1 , \四位二进制可逆计数器_1_q0 , \四位二进制可逆计数器_2_q1 , \四位二进制可逆计数器_2_q0 );
  not not_3 (not_3_out, ADj);
  D_Flip_Flop #(.trigger("falling")) d_ff_1 (.clk(CPu), .D(and_7_out), .Q(d_ff_1_q));  // open: Qn, preset, en, reset
  D_Flip_Flop #(.trigger("falling")) d_ff_2 (.clk(CPu), .D(and_8_out), .Q(d_ff_2_q));  // open: Qn, preset, en, reset
  and and_9 (Qcc, not_3_out, d_ff_1_q);
endmodule

module \_60以内八位二进制码转BCD码  (
  input  A7,
  input  A6,
  input  A5,
  input  A4,
  input  A3,
  input  A2,
  input  A1,
  input  A0,
  output A1D,
  output A1C,
  output A1B,
  output A1A,
  output A0D,
  output A0C,
  output A0B,
  output A0A
);

  wire and_1_out, and_2_out, and_3_out, and_4_out, and_5_out, and_6_out, and_7_out, and_8_out, and_9_out,
       and_10_out, and_11_out, and_12_out, and_13_out, and_14_out, and_15_out, and_16_out, and_17_out,
       and_18_out, and_19_out, and_20_out, and_21_out, and_22_out, and_23_out, and_24_out, and_25_out,
       and_26_out, and_27_out, and_28_out, and_29_out, and_30_out, and_31_out, and_32_out, and_33_out,
       and_34_out, and_35_out, and_36_out, and_37_out, and_38_out, not_1_out, not_2_out, not_3_out,
       not_4_out, not_5_out, not_6_out, not_7_out, not_8_out, not_9_out, not_10_out, not_11_out, not_12_out,
       not_13_out, not_14_out, not_15_out, not_16_out, not_17_out, not_18_out, not_19_out, not_20_out,
       not_21_out, not_22_out, not_23_out, not_24_out, not_25_out, not_26_out, not_27_out, not_28_out,
       not_29_out, not_30_out, not_31_out, not_32_out, not_33_out, not_34_out, not_35_out, not_36_out,
       not_37_out, not_38_out, not_39_out, not_40_out, not_41_out, not_42_out, not_43_out, not_44_out,
       not_45_out, not_46_out, not_47_out, not_48_out, not_49_out, not_50_out, not_51_out, not_52_out,
       not_53_out, not_54_out, not_55_out, not_56_out, not_57_out, not_58_out, not_59_out, not_60_out,
       not_61_out, not_62_out, not_63_out, not_64_out, not_65_out, not_66_out, not_67_out, not_68_out,
       not_69_out, not_70_out, not_71_out;

  not not_1 (not_1_out, A5);
  not not_2 (not_2_out, A5);
  not not_3 (not_3_out, A4);
  not not_4 (not_4_out, A3);
  not not_5 (not_5_out, A5);
  not not_6 (not_6_out, A4);
  not not_7 (not_7_out, A5);
  not not_8 (not_8_out, A4);
  not not_9 (not_9_out, A5);
  not not_10 (not_10_out, A5);
  not not_11 (not_11_out, A3);
  not not_12 (not_12_out, A2);
  not not_13 (not_13_out, A2);
  not not_14 (not_14_out, A5);
  not not_15 (not_15_out, A4);
  not not_16 (not_16_out, A2);
  not not_17 (not_17_out, A1);
  not not_18 (not_18_out, A5);
  not not_19 (not_19_out, A3);
  not not_20 (not_20_out, A2);
  not not_21 (not_21_out, A5);
  not not_22 (not_22_out, A1);
  not not_23 (not_23_out, A4);
  not not_24 (not_24_out, A3);
  not not_25 (not_25_out, A3);
  not not_26 (not_26_out, A2);
  not not_27 (not_27_out, A1);
  not not_28 (not_28_out, A2);
  not not_29 (not_29_out, A4);
  not not_30 (not_30_out, A3);
  not not_31 (not_31_out, A1);
  not not_32 (not_32_out, A5);
  not not_33 (not_33_out, A4);
  not not_34 (not_34_out, A5);
  not not_35 (not_35_out, A2);
  not not_36 (not_36_out, A1);
  not not_37 (not_37_out, A5);
  not not_38 (not_38_out, A2);
  not not_39 (not_39_out, A2);
  not not_40 (not_40_out, A1);
  not not_41 (not_41_out, A4);
  not not_42 (not_42_out, A3);
  not not_43 (not_43_out, A2);
  not not_44 (not_44_out, A4);
  not not_45 (not_45_out, A3);
  not not_46 (not_46_out, A5);
  not not_47 (not_47_out, A4);
  not not_48 (not_48_out, A3);
  not not_49 (not_49_out, A5);
  not not_50 (not_50_out, A3);
  not not_51 (not_51_out, A5);
  not not_52 (not_52_out, A4);
  not not_53 (not_53_out, A1);
  not not_54 (not_54_out, A5);
  not not_55 (not_55_out, A3);
  not not_56 (not_56_out, A2);
  not not_57 (not_57_out, A1);
  not not_58 (not_58_out, A5);
  not not_59 (not_59_out, A2);
  not not_60 (not_60_out, A4);
  not not_61 (not_61_out, A3);
  not not_62 (not_62_out, A1);
  not not_63 (not_63_out, A3);
  not not_64 (not_64_out, A1);
  not not_65 (not_65_out, A4);
  not not_66 (not_66_out, A2);
  not not_67 (not_67_out, A1);
  and and_1 (and_1_out, A5, A3);
  or or_1 (A1C, and_1_out, and_2_out);
  and and_2 (and_2_out, A5, A4);
  and and_3 (and_3_out, not_1_out, A4, A2);
  and and_4 (and_4_out, not_2_out, A4, A3);
  and and_5 (and_5_out, A4, A3, A2);
  and and_6 (and_6_out, A5, not_3_out, not_4_out);
  and and_7 (and_7_out, not_5_out, not_6_out, A3, A1);
  and and_8 (and_8_out, not_7_out, not_8_out, A3, A2);
  and and_9 (and_9_out, not_9_out, A3, A2, A1);
  and and_10 (and_10_out, not_10_out, A4, not_11_out, not_12_out);
  and and_11 (and_11_out, A5, not_68_out, not_69_out);
  not not_68 (not_68_out, A4);
  not not_69 (not_69_out, A3);
  not not_70 (not_70_out, A3);
  and and_12 (and_12_out, A5, not_70_out, A1);
  and and_13 (and_13_out, A5, not_71_out, A2);
  not not_71 (not_71_out, A3);
  and and_14 (and_14_out, A5, A4, A3, not_13_out);
  and and_15 (and_15_out, not_14_out, not_15_out, A3, not_16_out, not_17_out);
  and and_16 (and_16_out, not_18_out, A4, not_19_out, not_20_out, A1);
  and and_17 (and_17_out, not_21_out, A4, A3, A2, not_22_out);
  and and_18 (and_18_out, A5, not_23_out, not_24_out, A2, A1);
  and and_19 (and_19_out, A5, A4, not_25_out, not_26_out, not_27_out);
  and and_20 (and_20_out, A5, A4, A3, not_28_out, A1);
  and and_21 (and_21_out, not_29_out, not_30_out, A2, not_31_out);
  and and_22 (and_22_out, not_32_out, not_33_out, A2, A1);
  and and_23 (and_23_out, not_34_out, A4, not_35_out, not_36_out);
  and and_24 (and_24_out, not_37_out, A4, A3, not_38_out);
  and and_25 (and_25_out, A4, A3, not_39_out, not_40_out);
  and and_26 (and_26_out, A5, not_41_out, not_42_out, not_43_out, A1);
  and and_27 (and_27_out, A5, not_44_out, A3, A2);
  and and_28 (and_28_out, A5, A4, not_45_out, A2, A1);
  and and_29 (and_29_out, not_46_out, not_47_out, not_48_out, A1);
  and and_30 (and_30_out, not_49_out, not_50_out, A2, A1);
  and and_31 (and_31_out, not_51_out, not_52_out, A3, A2, not_53_out);
  and and_32 (and_32_out, not_54_out, A4, not_55_out, not_56_out, not_57_out);
  and and_33 (and_33_out, not_58_out, A4, A3, not_59_out, A1);
  and and_34 (and_34_out, A5, not_60_out, not_61_out, not_62_out);
  and and_35 (and_35_out, A5, not_63_out, A2, not_64_out);
  and and_36 (and_36_out, A5, not_65_out, A3, A1);
  and and_37 (and_37_out, A5, A3, A2, A1);
  and and_38 (and_38_out, A5, A4, A3, not_66_out, not_67_out);
  or or_2 (A1B, and_3_out, and_4_out, and_5_out, and_6_out);
  or or_3 (A1A, and_7_out, and_8_out, and_9_out, and_10_out, and_11_out, and_12_out, and_13_out, and_14_out);
  or or_4 (A0D, and_15_out, and_16_out, and_17_out, and_18_out, and_19_out, and_20_out);
  or or_5 (A0C, and_21_out, and_22_out, and_23_out, and_24_out, and_25_out, and_26_out, and_27_out, and_28_out);
  or or_6 (A0B, and_29_out, and_30_out, and_31_out, and_32_out, and_33_out, and_34_out, and_35_out, and_36_out, and_37_out, and_38_out);

  assign A0A = A0;
  assign A1D = 1'b0;
endmodule

module \十二进制计数器或二十四进制的计数器电路  (
  input  Set,
  input  CPu,
  input  ADj,
  input  CPd,
  input  Clr,
  output Q1D,
  output Q1C,
  output Q1B,
  output Q1A,
  output Q0D,
  output Q0C,
  output Q0B,
  output Q0A,
  output out_14
);

  wire and_1_out, and_2_out, and_3_out, d_ff_1_q, d_ff_2_q, nor_1_out, not_1_out, or_4_out, or_5_out,
       \六十进制计数器_1_q0b , \六十进制计数器_1_q1a ;

  nor nor_1 (nor_1_out, Q0D, Set, \六十进制计数器_1_q1a , Q0C, \六十进制计数器_1_q0b , Q0A);
  \六十进制计数器  \u_六十进制计数器_1  (
    .CPu(CPu), .CLR(and_1_out), .ADj(ADj), .CPd(CPd), .Q1D(Q1D), .Q0D(Q0D), .Q1C(Q1C), .Q0C(Q0C),
    .Q0B(\六十进制计数器_1_q0b ), .Q0A(Q0A), .Q1B(Q1B), .Q1A(\六十进制计数器_1_q1a ));  // open: Qcc
  or or_1 (Q1A, nor_1_out, \六十进制计数器_1_q1a );
  or or_2 (Q0B, nor_1_out, \六十进制计数器_1_q0b );
  not not_1 (not_1_out, Set);
  and and_1 (and_1_out, or_4_out, or_5_out);
  and and_2 (and_2_out, not_1_out, \六十进制计数器_1_q1a , Q0A);
  and and_3 (and_3_out, Q1B, Set, \六十进制计数器_1_q0b , Q0A);
  or or_3 (out_14, d_ff_2_q, d_ff_1_q);
  or or_4 (or_4_out, d_ff_2_q, Clr, d_ff_1_q);
  D_Flip_Flop #(.trigger("falling")) d_ff_1 (.clk(CPu), .D(and_2_out), .Q(d_ff_1_q));  // open: Qn, preset, en, reset
  D_Flip_Flop #(.trigger("falling")) d_ff_2 (.clk(CPu), .D(and_3_out), .Q(d_ff_2_q));  // open: Qn, preset, en, reset
  or or_5 (or_5_out, Q0D, Q0C, \六十进制计数器_1_q0b , Q0A);
endmodule

module \十二进制计数器或二十四进制的计数器测试电路  (
  input  in_1,
  input  in_2,
  input  in_3,
  output out_4
);

  wire button_1_out, button_2_out;
  wire [3:0] \十二进制计数器或二十四进制的计数器电路_1_q0a , \十二进制计数器或二十四进制的计数器电路_1_q1a ;

  Button button_1 (.out(button_1_out));
  Button button_2 (.out(button_2_out));
  Hex_Digit_Display hex_digit_display_1 (.value(\十二进制计数器或二十四进制的计数器电路_1_q1a ));  // open: dp
  \十二进制计数器或二十四进制的计数器电路  \u_十二进制计数器或二十四进制的计数器电路_1  (
    .Set(in_2), .CPu(button_1_out), .ADj(in_1), .CPd(button_2_out), .Clr(in_3),
    .Q1D(\十二进制计数器或二十四进制的计数器电路_1_q1a [3]), .Q1C(\十二进制计数器或二十四进制的计数器电路_1_q1a [2]),
    .Q1B(\十二进制计数器或二十四进制的计数器电路_1_q1a [1]), .Q1A(\十二进制计数器或二十四进制的计数器电路_1_q1a [0]),
    .Q0D(\十二进制计数器或二十四进制的计数器电路_1_q0a [3]), .Q0C(\十二进制计数器或二十四进制的计数器电路_1_q0a [2]),
    .Q0B(\十二进制计数器或二十四进制的计数器电路_1_q0a [1]), .Q0A(\十二进制计数器或二十四进制的计数器电路_1_q0a [0]), .out_14(out_4));
  Hex_Digit_Display hex_digit_display_2 (.value(\十二进制计数器或二十四进制的计数器电路_1_q0a ));  // open: dp
endmodule

module \上下午文字显示电路  (
  input  TT,
  input  AM_FM,
  output [4:0] A0,
  output [4:0] A1,
  output [4:0] A2,
  output [4:0] A3
);

  wire [19:0] multiplexer_2_out;

  Multiplexer #(.width(20), .enable("false")) multiplexer_1 (
    .in0({20{1'b0}}), .in1(multiplexer_2_out), .out({A3, A2, A1, A0}), .sel(TT));
  Multiplexer #(.width(20), .enable("false")) multiplexer_2 (
    .in0(20'hfca1), .in1(20'h87e90), .out(multiplexer_2_out), .sel(AM_FM));
endmodule

module \上下午文字显示测试电路  (
  input  in_1,
  input  in_2
);

  wire [4:0] \上下午文字显示电路_1_a0 , \上下午文字显示电路_1_a1 , \上下午文字显示电路_1_a2 , \上下午文字显示电路_1_a3 ;

  DotMatrix #(.matrixcols(4), .matrixrows(5)) dotmatrix_1 (
    .col0(\上下午文字显示电路_1_a3 ), .col1(\上下午文字显示电路_1_a2 ), .col2(\上下午文字显示电路_1_a1 ), .col3(\上下午文字显示电路_1_a0 ));
  \上下午文字显示电路  \u_上下午文字显示电路_1  (
    .TT(in_2), .AM_FM(in_1), .A0(\上下午文字显示电路_1_a0 ), .A1(\上下午文字显示电路_1_a1 ), .A2(\上下午文字显示电路_1_a2 ),
    .A3(\上下午文字显示电路_1_a3 ));
endmodule

module \电子钟整点报时电路  (
  input  [7:0] M,
  input  CPu,
  input  [7:0] S,
  output out_4
);

  wire comparator_1_eq, comparator_2_gt;

  Comparator comparator_1 (.a(M), .b(8'h59), .eq(comparator_1_eq));  // open: gt, lt
  Comparator comparator_2 (.a(S), .b(8'h49), .gt(comparator_2_gt));  // open: eq, lt
  and and_1 (out_4, comparator_1_eq, CPu, comparator_2_gt);
endmodule

module \电子钟整点报时测试电路  (
  input  [7:0] in_1,
  input  [7:0] in_2
);

  wire button_1_out, \电子钟整点报时电路_1_out_4 ;

  Button button_1 (.out(button_1_out));
  \电子钟整点报时电路  \u_电子钟整点报时电路_1  (.CPu(button_1_out), .M(in_1), .S(in_2), .out_4(\电子钟整点报时电路_1_out_4 ));
  LED led_1 (.in(\电子钟整点报时电路_1_out_4 ));
endmodule

module \秒计时脉冲产生电路  (
  input  in_1,
  output out_2
);

  wire t_ff_1_q;

  T_Flip_Flop t_ff_1 (.clk(in_1), .T(1'b1), .Q(t_ff_1_q));  // open: Qn, preset, reset, en
  T_Flip_Flop t_ff_2 (.clk(t_ff_1_q), .T(1'b1), .Q(out_2));  // open: Qn, preset, reset, en
endmodule

module \秒计时脉冲产生测试电路  (
);

  wire clock_1_out, \秒计时脉冲产生电路_1_out_2 ;

  Clock clock_1 (.out(clock_1_out));
  \秒计时脉冲产生电路  \u_秒计时脉冲产生电路_1  (.in_1(clock_1_out), .out_2(\秒计时脉冲产生电路_1_out_2 ));
  Clock clock_2 (.out(\秒计时脉冲产生电路_1_out_2 ));
endmodule

module \多功能数字钟电路  (
  input  CP,
  input  CLR,
  input  Adj1,
  input  Adj0,
  input  CPd,
  input  CPu,
  input  Set,
  output [3:0] H1,
  output [3:0] H0,
  output [3:0] S1,
  output [3:0] S0,
  output \报时 ,
  output [3:0] M1,
  output [3:0] M0,
  output [4:0] A3,
  output [4:0] A2,
  output [4:0] A1,
  output [4:0] A0
);

  wire and_1_out, and_2_out, and_3_out, and_4_out, and_5_out, and_6_out, and_7_out, comparator_1_eq,
       comparator_2_gt, comparator_3_eq, comparator_4_eq, comparator_5_eq, multiplexer_1_out,
       multiplexer_2_out, not_1_out, not_2_out, not_3_out, \六十进制计数器_1_qcc , \六十进制计数器_2_qcc ,
       \十二进制计数器或二十四进制的计数器电路_1_out_14 , \秒计时脉冲产生电路_1_out_2 ;
  wire [3:0] multiplexer_9_out, \十二进制计数器或二十四进制的计数器电路_1_q0a , \十二进制计数器或二十四进制的计数器电路_1_q1a ;
  wire [7:0] multiplexer_6_out, multiplexer_7_out, multiplexer_8_out, subtractor_1_out;
  wire [7:4] multiplexer_9_out_2;

  \秒计时脉冲产生电路  \u_秒计时脉冲产生电路_1  (.in_1(CP), .out_2(\秒计时脉冲产生电路_1_out_2 ));
  not not_1 (not_1_out, Adj0);
  and and_1 (and_1_out, \秒计时脉冲产生电路_1_out_2 , not_1_out);
  \六十进制计数器  \u_六十进制计数器_1  (
    .CPu(and_1_out), .CLR(CLR), .ADj(1'b0), .CPd(1'b0), .Q1D(S1[3]), .Q0D(S0[3]), .Q1C(S1[2]), .Q0C(S0[2]),
    .Q0B(S0[1]), .Q0A(S0[0]), .Q1B(S1[1]), .Q1A(S1[0]), .Qcc(\六十进制计数器_1_qcc ));
  and and_2 (and_2_out, CPu, and_3_out);
  and and_3 (and_3_out, Adj1, Adj0);
  \电子钟整点报时电路  \u_电子钟整点报时电路_1  (.CPu(\秒计时脉冲产生电路_1_out_2 ), .M({M1, M0}), .S({S1, S0}), .out_4(\报时 ));
  Multiplexer multiplexer_1 (
    .in0(\六十进制计数器_1_qcc ), .in1(and_2_out), .out(multiplexer_1_out), .sel(and_3_out));  // open: en
  \六十进制计数器  \u_六十进制计数器_2  (
    .CPu(multiplexer_1_out), .CLR(CLR), .ADj(and_3_out), .CPd(CPd), .Q1D(M1[3]), .Q0D(M0[3]), .Q1C(M1[2]),
    .Q0C(M0[2]), .Q0B(M0[1]), .Q0A(M0[0]), .Q1B(M1[1]), .Q1A(M1[0]), .Qcc(\六十进制计数器_2_qcc ));
  Comparator comparator_1 (.a(multiplexer_6_out), .b({8{1'b0}}), .eq(comparator_1_eq));  // open: gt, lt
  and and_4 (and_4_out, CPu, and_5_out);
  and and_5 (and_5_out, not_2_out, Adj0);
  not not_2 (not_2_out, Adj1);
  not not_3 (not_3_out, Set);
  and and_6 (and_6_out, not_3_out, comparator_1_eq);
  Multiplexer multiplexer_2 (
    .in0(\六十进制计数器_2_qcc ), .in1(and_4_out), .out(multiplexer_2_out), .sel(and_5_out));  // open: en
  Multiplexer #(.width(4)) multiplexer_3 (
    .in0(multiplexer_6_out[7:4]), .in1(4'b0001), .out(H1), .sel(and_6_out));  // open: en
  Multiplexer #(.width(4)) multiplexer_4 (
    .in0(\十二进制计数器或二十四进制的计数器电路_1_q1a ), .in1(multiplexer_9_out_2), .out(multiplexer_6_out[7:4]),
    .sel(and_7_out));  // open: en
  \十二进制计数器或二十四进制的计数器电路  \u_十二进制计数器或二十四进制的计数器电路_1  (
    .Set(1'b1), .CPu(multiplexer_2_out), .ADj(and_5_out), .CPd(CPd), .Clr(CLR),
    .Q1D(\十二进制计数器或二十四进制的计数器电路_1_q1a [3]), .Q1C(\十二进制计数器或二十四进制的计数器电路_1_q1a [2]),
    .Q1B(\十二进制计数器或二十四进制的计数器电路_1_q1a [1]), .Q1A(\十二进制计数器或二十四进制的计数器电路_1_q1a [0]),
    .Q0D(\十二进制计数器或二十四进制的计数器电路_1_q0a [3]), .Q0C(\十二进制计数器或二十四进制的计数器电路_1_q0a [2]),
    .Q0B(\十二进制计数器或二十四进制的计数器电路_1_q0a [1]), .Q0A(\十二进制计数器或二十四进制的计数器电路_1_q0a [0]),
    .out_14(\十二进制计数器或二十四进制的计数器电路_1_out_14 ));
  Multiplexer #(.width(4)) multiplexer_5 (
    .in0(multiplexer_6_out[3:0]), .in1(4'b0010), .out(H0), .sel(and_6_out));  // open: en
  Multiplexer #(.width(4)) multiplexer_6 (
    .in0(\十二进制计数器或二十四进制的计数器电路_1_q0a ), .in1(multiplexer_9_out), .out(multiplexer_6_out[3:0]), .sel(and_7_out));  // open: en
  and and_7 (and_7_out, not_3_out, comparator_2_gt);
  Subtractor subtractor_1 (
    .a({\十二进制计数器或二十四进制的计数器电路_1_q1a , \十二进制计数器或二十四进制的计数器电路_1_q0a }), .b(8'h12), .out(subtractor_1_out));  // open: bin, bout
  Comparator comparator_2 (
    .a({\十二进制计数器或二十四进制的计数器电路_1_q1a , \十二进制计数器或二十四进制的计数器电路_1_q0a }), .b(8'h11), .gt(comparator_2_gt));  // open: eq, lt
  Comparator comparator_3 (.a(subtractor_1_out), .b(8'hf), .eq(comparator_3_eq));  // open: gt, lt
  Comparator comparator_4 (.a(subtractor_1_out), .b(8'he), .eq(comparator_4_eq));  // open: gt, lt
  Comparator comparator_5 (.a(subtractor_1_out), .b({8{1'b0}}), .eq(comparator_5_eq));  // open: gt, lt
  Multiplexer #(.width(8)) multiplexer_7 (
    .in0(subtractor_1_out), .in1(8'h9), .out(multiplexer_7_out), .sel(comparator_3_eq));  // open: en
  Multiplexer #(.width(8)) multiplexer_8 (
    .in0(multiplexer_7_out), .in1(8'h8), .out(multiplexer_8_out), .sel(comparator_4_eq));  // open: en
  Multiplexer #(.width(8)) multiplexer_9 (
    .in0(multiplexer_8_out), .in1(8'h12), .out({multiplexer_9_out_2, multiplexer_9_out}),
    .sel(comparator_5_eq));  // open: en
  \上下午文字显示电路  \u_上下午文字显示电路_1  (.TT(not_3_out), .AM_FM(comparator_2_gt), .A0(A0), .A1(A1), .A2(A2), .A3(A3));
endmodule

module \多功能数字钟测试电路  (
  input  in_1,
  input  in_2,
  input  in_3,
  input  in_4
);

  wire button_1_out, button_2_out, clock_1_out, \多功能数字钟电路_1_报时 ;
  wire [3:0] \多功能数字钟电路_1_h0 , \多功能数字钟电路_1_h1 , \多功能数字钟电路_1_m0 , \多功能数字钟电路_1_m1 , \多功能数字钟电路_1_s0 ,
       \多功能数字钟电路_1_s1 ;
  wire [4:0] \多功能数字钟电路_1_a0 , \多功能数字钟电路_1_a1 , \多功能数字钟电路_1_a2 , \多功能数字钟电路_1_a3 ;

  DotMatrix #(.matrixcols(4), .matrixrows(5)) dotmatrix_1 (
    .col0(\多功能数字钟电路_1_a3 ), .col1(\多功能数字钟电路_1_a2 ), .col2(\多功能数字钟电路_1_a1 ), .col3(\多功能数字钟电路_1_a0 ));
  \多功能数字钟电路  \u_多功能数字钟电路_1  (
    .CP(clock_1_out), .CLR(in_4), .Adj1(in_2), .Adj0(in_1), .CPd(button_1_out), .CPu(button_2_out),
    .Set(in_3), .S1(\多功能数字钟电路_1_s1 ), .S0(\多功能数字钟电路_1_s0 ), .M1(\多功能数字钟电路_1_m1 ), .M0(\多功能数字钟电路_1_m0 ),
    .H1(\多功能数字钟电路_1_h1 ), .H0(\多功能数字钟电路_1_h0 ), .\报时 (\多功能数字钟电路_1_报时 ), .A2(\多功能数字钟电路_1_a2 ),
    .A1(\多功能数字钟电路_1_a1 ), .A0(\多功能数字钟电路_1_a0 ), .A3(\多功能数字钟电路_1_a3 ));
  Clock clock_1 (.out(clock_1_out));
  Hex_Digit_Display hex_digit_display_1 (.value(\多功能数字钟电路_1_h0 ));  // open: dp
  Hex_Digit_Display hex_digit_display_2 (.value(\多功能数字钟电路_1_h1 ));  // open: dp
  Button button_1 (.out(button_1_out));
  Button button_2 (.out(button_2_out));
  Hex_Digit_Display hex_digit_display_3 (.value(\多功能数字钟电路_1_m1 ));  // open: dp
  Hex_Digit_Display hex_digit_display_4 (.value(\多功能数字钟电路_1_m0 ));  // open: dp
  Hex_Digit_Display hex_digit_display_5 (.value(\多功能数字钟电路_1_s0 ));  // open: dp
  Hex_Digit_Display hex_digit_display_6 (.value(\多功能数字钟电路_1_s1 ));  // open: dp
  LED led_1 (.in(\多功能数字钟电路_1_报时 ));
endmodule
