// Logisim project 实验6-CS190X-U2019XXXXX-XX.circ as structural Verilog: 7 circuits, main circuit sqrX
module sqrX (
  input  [31:0] a,
  input  [31:0] b,
  input  [31:0] c,
  input  [31:0] in_4,
  output [31:0] a_prime,
  output [31:0] b_prime,
  output [31:0] c_prime,
  output [31:0] d_prime
);

  wire [31:0] multiplier_1_out, multiplier_2_out, multiplier_3_out, multiplier_4_out, multiplier_5_out,
       multiplier_6_out, multiplier_7_out, multiplier_8_out;

  Multiplier #(.width(32)) multiplier_1 (.a(a), .b(a), .out(multiplier_1_out));  // open: cin, cout
  Multiplier #(.width(32)) multiplier_2 (.a(b), .b(c), .out(multiplier_2_out));  // open: cin, cout
  Multiplier #(.width(32)) multiplier_3 (.a(a), .b(b), .out(multiplier_3_out));  // open: cin, cout
  Multiplier #(.width(32)) multiplier_4 (.a(b), .b(in_4), .out(multiplier_4_out));  // open: cin, cout
  Multiplier #(.width(32)) multiplier_5 (.a(a), .b(c), .out(multiplier_5_out));  // open: cin, cout
  Multiplier #(.width(32)) multiplier_6 (.a(c), .b(in_4), .out(multiplier_6_out));  // open: cin, cout
  Multiplier #(.width(32)) multiplier_7 (.a(b), .b(c), .out(multiplier_7_out));  // open: cin, cout
  Multiplier #(.width(32)) multiplier_8 (.a(in_4), .b(in_4), .out(multiplier_8_out));  // open: cin, cout
  Adder #(.width(32)) adder_1 (.a(multiplier_1_out), .b(multiplier_2_out), .out(a_prime));  // open: cin, cout
  Adder #(.width(32)) adder_2 (.a(multiplier_3_out), .b(multiplier_4_out), .out(b_prime));  // open: cin, cout
  Adder #(.width(32)) adder_3 (.a(multiplier_5_out), .b(multiplier_6_out), .out(c_prime));  // open: cin, cout
  Adder #(.width(32)) adder_4 (.a(multiplier_7_out), .b(multiplier_8_out), .out(d_prime));  // open: cin, cout
endmodule

module sqrX_A (
  input  [31:0] a,
  input  [31:0] b,
  input  [31:0] c,
  input  [31:0] in_4,
  output [31:0] a_prime_prime,
  output [31:0] b_prime_prime,
  output [31:0] c_prime_prime,
  output [31:0] d_prime_prime
);

  wire [31:0] adder_2_out, adder_3_out, adder_5_out, adder_6_out, multiplier_1_out, multiplier_2_out,
       multiplier_3_out, multiplier_4_out, multiplier_5_out, multiplier_6_out, multiplier_7_out,
       multiplier_8_out, multiplier_9_out, multiplier_10_out, multiplier_11_out, multiplier_12_out;

  Multiplier #(.width(32)) multiplier_1 (.a(a), .b(b), .out(multiplier_1_out));  // open: cin, cout
  Multiplier #(.width(32)) multiplier_2 (.a(b), .b(in_4), .out(multiplier_2_out));  // open: cin, cout
  Multiplier #(.width(32)) multiplier_3 (.a(a), .b(a), .out(multiplier_3_out));  // open: cin, cout
  Multiplier #(.width(32)) multiplier_4 (.a(b), .b(c), .out(multiplier_4_out));  // open: cin, cout
  Multiplier #(.width(32)) multiplier_5 (.a(a), .b(b), .out(multiplier_5_out));  // open: cin, cout
  Multiplier #(.width(32)) multiplier_6 (.a(b), .b(in_4), .out(multiplier_6_out));  // open: cin, cout
  Multiplier #(.width(32)) multiplier_7 (.a(c), .b(b), .out(multiplier_7_out));  // open: cin, cout
  Multiplier #(.width(32)) multiplier_8 (.a(in_4), .b(in_4), .out(multiplier_8_out));  // open: cin, cout
  Multiplier #(.width(32)) multiplier_9 (.a(a), .b(c), .out(multiplier_9_out));  // open: cin, cout
  Multiplier #(.width(32)) multiplier_10 (.a(c), .b(in_4), .out(multiplier_10_out));  // open: cin, cout
  Multiplier #(.width(32)) multiplier_11 (.a(in_4), .b(in_4), .out(multiplier_11_out));  // open: cin, cout
  Multiplier #(.width(32)) multiplier_12 (.a(b), .b(c), .out(multiplier_12_out));  // open: cin, cout
  Adder #(.width(32)) adder_1 (.a(multiplier_1_out), .b(multiplier_2_out), .out(a_prime_prime));  // open: cin, cout
  Adder #(.width(32)) adder_2 (.a(multiplier_3_out), .b(multiplier_4_out), .out(adder_2_out));  // open: cin, cout
  Adder #(.width(32)) adder_3 (.a(multiplier_5_out), .b(multiplier_6_out), .out(adder_3_out));  // open: cin, cout
  Adder #(.width(32)) adder_4 (.a(multiplier_7_out), .b(multiplier_8_out), .out(c_prime_prime));  // open: cin, cout
  Adder #(.width(32)) adder_5 (.a(multiplier_9_out), .b(multiplier_10_out), .out(adder_5_out));  // open: cin, cout
  Adder #(.width(32)) adder_6 (.a(multiplier_11_out), .b(multiplier_12_out), .out(adder_6_out));  // open: cin, cout
  Adder #(.width(32)) adder_7 (.a(adder_2_out), .b(adder_3_out), .out(b_prime_prime));  // open: cin, cout
  Adder #(.width(32)) adder_8 (.a(adder_5_out), .b(adder_6_out), .out(d_prime_prime));  // open: cin, cout
endmodule

module \矩阵快速幂算法迭代模块  (
  input  start,
  input  clear,
  input  clk,
  input  ni_1,
  output [31:0] Fi
);

  wire and_1_out, not_1_out, or_1_out;
  wire [31:0] multiplexer_1_out, multiplexer_2_out, multiplexer_3_out, multiplexer_4_out, multiplexer_5_out,
       multiplexer_6_out, multiplexer_7_out, multiplexer_8_out, register_1_q, register_3_q, register_4_q,
       sqrx_1_a_prime, sqrx_1_b_prime, sqrx_1_c_prime, sqrx_1_d_prime, sqrx_a_1_a_prime_prime,
       sqrx_a_1_b_prime_prime, sqrx_a_1_c_prime_prime, sqrx_a_1_d_prime_prime;

  not not_1 (not_1_out, clear);
  and and_1 (and_1_out, start, not_1_out);
  or or_1 (or_1_out, clear, clk);
  Multiplexer #(.width(32), .enable("false")) multiplexer_1 (
    .in0({32{1'b0}}), .in1(multiplexer_5_out), .out(multiplexer_1_out), .sel(and_1_out));
  Multiplexer #(.width(32), .enable("false")) multiplexer_2 (
    .in0(32'h1), .in1(multiplexer_6_out), .out(multiplexer_2_out), .sel(and_1_out));
  Multiplexer #(.width(32), .enable("false")) multiplexer_3 (
    .in0(32'h1), .in1(multiplexer_7_out), .out(multiplexer_3_out), .sel(and_1_out));
  Multiplexer #(.width(32), .enable("false")) multiplexer_4 (
    .in0(32'h1), .in1(multiplexer_8_out), .out(multiplexer_4_out), .sel(and_1_out));
  Register #(.width(32), .trigger("falling")) register_1 (
    .D(multiplexer_1_out), .Q(register_1_q), .clk(or_1_out));  // open: en, clr
  Register #(.width(32), .trigger("falling")) register_2 (
    .D(multiplexer_2_out), .Q(Fi), .clk(or_1_out));  // open: en, clr
  Register #(.width(32), .trigger("falling")) register_3 (
    .D(multiplexer_3_out), .Q(register_3_q), .clk(or_1_out));  // open: en, clr
  Register #(.width(32), .trigger("falling")) register_4 (
    .D(multiplexer_4_out), .Q(register_4_q), .clk(or_1_out));  // open: en, clr
  sqrX sqrx_1 (
    .a(register_1_q), .b(Fi), .c(register_3_q), .in_4(register_4_q), .a_prime(sqrx_1_a_prime),
    .b_prime(sqrx_1_b_prime), .c_prime(sqrx_1_c_prime), .d_prime(sqrx_1_d_prime));
  sqrX_A sqrx_a_1 (
    .a(register_1_q), .b(Fi), .c(register_3_q), .in_4(register_4_q), .a_prime_prime(sqrx_a_1_a_prime_prime),
    .b_prime_prime(sqrx_a_1_b_prime_prime), .c_prime_prime(sqrx_a_1_c_prime_prime),
    .d_prime_prime(sqrx_a_1_d_prime_prime));
  Multiplexer #(.width(32), .enable("false")) multiplexer_5 (
    .in0(sqrx_1_a_prime), .in1(sqrx_a_1_a_prime_prime), .out(multiplexer_5_out), .sel(ni_1));
  Multiplexer #(.width(32), .enable("false")) multiplexer_6 (
    .in0(sqrx_1_b_prime), .in1(sqrx_a_1_b_prime_prime), .out(multiplexer_6_out), .sel(ni_1));
  Multiplexer #(.width(32), .enable("false")) multiplexer_7 (
    .in0(sqrx_1_c_prime), .in1(sqrx_a_1_c_prime_prime), .out(multiplexer_7_out), .sel(ni_1));
  Multiplexer #(.width(32), .enable("false")) multiplexer_8 (
    .in0(sqrx_1_d_prime), .in1(sqrx_a_1_d_prime_prime), .out(multiplexer_8_out), .sel(ni_1));
endmodule

module \Fibonacci数显示模块  (
  input  [31:0] Fn,
  output [3:0] D0,
  output [3:0] D1,
  output [3:0] D2,
  output [3:0] D3,
  output [3:0] D4,
  output [3:0] D5,
  output [3:0] D6,
  output [3:0] D7,
  output [3:0] D8,
  output [3:0] D9
);

  wire [31:0] divider_1_out, divider_2_out, divider_3_out, divider_4_out, divider_5_out, divider_6_out,
       divider_7_out, divider_8_out, divider_9_out;
  wire [31:4] divider_1_rem, divider_2_rem, divider_3_rem, divider_4_rem, divider_5_rem, divider_6_rem,
       divider_7_rem, divider_8_rem, divider_9_rem, divider_10_rem;

  Divider #(.width(32)) divider_1 (
    .a(Fn), .b(32'ha), .out(divider_1_out), .upper({32{1'b0}}), .rem({divider_1_rem, D0}));
  Divider #(.width(32)) divider_2 (
    .a(divider_1_out), .b(32'ha), .out(divider_2_out), .upper({32{1'b0}}), .rem({divider_2_rem, D1}));
  Divider #(.width(32)) divider_3 (
    .a(divider_2_out), .b(32'ha), .out(divider_3_out), .upper({32{1'b0}}), .rem({divider_3_rem, D2}));
  Divider #(.width(32)) divider_4 (
    .a(divider_3_out), .b(32'ha), .out(divider_4_out), .upper({32{1'b0}}), .rem({divider_4_rem, D3}));
  Divider #(.width(32)) divider_5 (
    .a(divider_4_out), .b(32'ha), .out(divider_5_out), .upper({32{1'b0}}), .rem({divider_5_rem, D4}));
  Divider #(.width(32)) divider_6 (
    .a(divider_5_out), .b(32'ha), .out(divider_6_out), .upper({32{1'b0}}), .rem({divider_6_rem, D5}));
  Divider #(.width(32)) divider_7 (
    .a(divider_6_out), .b(32'ha), .out(divider_7_out), .upper({32{1'b0}}), .rem({divider_7_rem, D6}));
  Divider #(.width(32)) divider_8 (
    .a(divider_7_out), .b(32'ha), .out(divider_8_out), .upper({32{1'b0}}), .rem({divider_8_rem, D7}));
  Divider #(.width(32)) divider_9 (
    .a(divider_8_out), .b(32'ha), .out(divider_9_out), .upper({32{1'b0}}), .rem({divider_9_rem, D8}));
  Divider #(.width(32)) divider_10 (
    .a(divider_9_out), .b(32'ha), .upper({32{1'b0}}), .rem({divider_10_rem, D9}));  // open: out
endmodule

module \控制器  (
  input  [5:0] n,
  input  clear,
  input  clock,
  output start,
  output ni_1,
  output clk,
  output clear_2
);

  wire comparator_1_lt, d_ff_1_q, not_1_out, or_1_out, shift_register_1_out;
  wire [7:0] counter_1_q;

  not not_1 (not_1_out, clear);
  or or_1 (or_1_out, clear, clock);
  Shift_Register #(.length(7)) shift_register_1 (
    .shift(not_1_out), .in(1'b0), .clk(or_1_out), .out(shift_register_1_out), .load(clear), .d0(n[0]),
    .d1(n[1]), .d2(n[2]), .d3(n[3]), .d4(n[4]), .d5(n[5]), .d6(1'b0), .q6(ni_1));  // open: clr, q0, q1, q2, q3, q4, q5
  Counter #(.ongoal("stay")) counter_1 (
    .count(1'b1), .Q(counter_1_q), .clk(clock), .clr(clear));  // open: load, D, carry
  Comparator comparator_1 (.a(counter_1_q), .b(8'h6), .lt(comparator_1_lt));  // open: gt, eq
  D_Flip_Flop d_ff_1 (.Q(d_ff_1_q), .preset(shift_register_1_out), .reset(clear));  // open: clk, D, Qn, en
  and and_1 (clk, comparator_1_lt, clock);
  Register #(.width(1)) register_1 (.D(d_ff_1_q), .Q(start), .clk(clock), .clr(clear));  // open: en

  assign clear_2 = clear;
endmodule

module \斐波那契_Fibonacci_数列计算器  (
  input  [5:0] in_1,
  input  in_2
);

  wire clock_1_out, \控制器_1_clear_2 , \控制器_1_clk , \控制器_1_ni_1 , \控制器_1_start ;
  wire [3:0] \fibonacci数显示模块_1_d0 , \fibonacci数显示模块_1_d1 , \fibonacci数显示模块_1_d2 , \fibonacci数显示模块_1_d3 ,
       \fibonacci数显示模块_1_d4 , \fibonacci数显示模块_1_d5 , \fibonacci数显示模块_1_d6 , \fibonacci数显示模块_1_d7 ,
       \fibonacci数显示模块_1_d8 , \fibonacci数显示模块_1_d9 ;
  wire [31:0] \矩阵快速幂算法迭代模块_1_fi ;

  Clock clock_1 (.out(clock_1_out));
  \控制器  \u_控制器_1  (
    .n(in_1), .clear(in_2), .clock(clock_1_out), .start(\控制器_1_start ), .ni_1(\控制器_1_ni_1 ),
    .clk(\控制器_1_clk ), .clear_2(\控制器_1_clear_2 ));
  \矩阵快速幂算法迭代模块  \u_矩阵快速幂算法迭代模块_1  (
    .start(\控制器_1_start ), .clear(\控制器_1_clear_2 ), .clk(\控制器_1_clk ), .ni_1(\控制器_1_ni_1 ),
    .Fi(\矩阵快速幂算法迭代模块_1_fi ));
  Hex_Digit_Display hex_digit_display_1 (.value(\fibonacci数显示模块_1_d9 ));  // open: dp
  Hex_Digit_Display hex_digit_display_2 (.value(\fibonacci数显示模块_1_d8 ));  // open: dp
  \Fibonacci数显示模块  \fibonacci数显示模块_1  (
    .Fn(\矩阵快速幂算法迭代模块_1_fi ), .D0(\fibonacci数显示模块_1_d0 ), .D1(\fibonacci数显示模块_1_d1 ),
    .D2(\fibonacci数显示模块_1_d2 ), .D3(\fibonacci数显示模块_1_d3 ), .D4(\fibonacci数显示模块_1_d4 ),
    .D5(\fibonacci数显示模块_1_d5 ), .D6(\fibonacci数显示模块_1_d6 ), .D7(\fibonacci数显示模块_1_d7 ),
    .D8(\fibonacci数显示模块_1_d8 ), .D9(\fibonacci数显示模块_1_d9 ));
  Hex_Digit_Display hex_digit_display_3 (.value(\fibonacci数显示模块_1_d7 ));  // open: dp
  Hex_Digit_Display hex_digit_display_4 (.value(\fibonacci数显示模块_1_d6 ));  // open: dp
  Hex_Digit_Display hex_digit_display_5 (.value(\fibonacci数显示模块_1_d5 ));  // open: dp
  Hex_Digit_Display hex_digit_display_6 (.value(\fibonacci数显示模块_1_d4 ));  // open: dp
  Hex_Digit_Display hex_digit_display_7 (.value(\fibonacci数显示模块_1_d2 ));  // open: dp
  Hex_Digit_Display hex_digit_display_8 (.value(\fibonacci数显示模块_1_d3 ));  // open: dp
  Hex_Digit_Display hex_digit_display_9 (.value(\fibonacci数显示模块_1_d1 ));  // open: dp
  Hex_Digit_Display hex_digit_display_10 (.value(\fibonacci数显示模块_1_d0 ));  // open: dp
endmodule

module \斐波那契_Fibonacci_数列计算器验证电路  (
  input  [5:0] in_1
);

  wire button_1_out, button_2_out, \控制器_1_clear_2 , \控制器_1_clk , \控制器_1_ni_1 , \控制器_1_start ;
  wire [3:0] \fibonacci数显示模块_1_d0 , \fibonacci数显示模块_1_d1 , \fibonacci数显示模块_1_d2 , \fibonacci数显示模块_1_d3 ,
       \fibonacci数显示模块_1_d4 , \fibonacci数显示模块_1_d5 , \fibonacci数显示模块_1_d6 , \fibonacci数显示模块_1_d7 ,
       \fibonacci数显示模块_1_d8 , \fibonacci数显示模块_1_d9 ;
  wire [31:0] \矩阵快速幂算法迭代模块_1_fi ;

  Button button_1 (.out(button_1_out));
  Button button_2 (.out(button_2_out));
  \控制器  \u_控制器_1  (
    .n(in_1), .clear(button_1_out), .clock(button_2_out), .start(\控制器_1_start ), .ni_1(\控制器_1_ni_1 ),
    .clk(\控制器_1_clk ), .clear_2(\控制器_1_clear_2 ));
  \矩阵快速幂算法迭代模块  \u_矩阵快速幂算法迭代模块_1  (
    .start(\控制器_1_start ), .clear(\控制器_1_clear_2 ), .clk(\控制器_1_clk ), .ni_1(\控制器_1_ni_1 ),
    .Fi(\矩阵快速幂算法迭代模块_1_fi ));
  Hex_Digit_Display hex_digit_display_1 (.value(\fibonacci数显示模块_1_d9 ));  // open: dp
  Hex_Digit_Display hex_digit_display_2 (.value(\fibonacci数显示模块_1_d8 ));  // open: dp
  \Fibonacci数显示模块  \fibonacci数显示模块_1  (
    .Fn(\矩阵快速幂算法迭代模块_1_fi ), .D0(\fibonacci数显示模块_1_d0 ), .D1(\fibonacci数显示模块_1_d1 ),
    .D2(\fibonacci数显示模块_1_d2 ), .D3(\fibonacci数显示模块_1_d3 ), .D4(\fibonacci数显示模块_1_d4 ),
    .D5(\fibonacci数显示模块_1_d5 ), .D6(\fibonacci数显示模块_1_d6 ), .D7(\fibonacci数显示模块_1_d7 ),
    .D8(\fibonacci数显示模块_1_d8 ), .D9(\fibonacci数显示模块_1_d9 ));
  Hex_Digit_Display hex_digit_display_3 (.value(\fibonacci数显示模块_1_d7 ));  // open: dp
  Hex_Digit_Display hex_digit_display_4 (.value(\fibonacci数显示模块_1_d5 ));  // open: dp
  Hex_Digit_Display hex_digit_display_5 (.value(\fibonacci数显示模块_1_d6 ));  // open: dp
  Hex_Digit_Display hex_digit_display_6 (.value(\fibonacci数显示模块_1_d4 ));  // open: dp
  Hex_Digit_Display hex_digit_display_7 (.value(\fibonacci数显示模块_1_d3 ));  // open: dp
  Hex_Digit_Display hex_digit_display_8 (.value(\fibonacci数显示模块_1_d2 ));  // open: dp
  Hex_Digit_Display hex_digit_display_9 (.value(\fibonacci数显示模块_1_d1 ));  // open: dp
  Hex_Digit_Display hex_digit_display_10 (.value(\fibonacci数显示模块_1_d0 ));  // open: dp
endmodule
